# Fritzing sketch SWMS (saved by Fritzing 0.9.3b)

parts:
  U1 = NodeMCU V1.0
  OLED1 = OLED 128x64 I2C Monochrome Display VDD-GND
  PIR1 = PIR sensor
  A1 = yf-s401 flow sensor [package=THT]

nets:
  N1: U1.D1, OLED1.SCK
  N2: U1.D2, OLED1.SDA
  N3: U1.D4, A1.pin3
  VDD: U1.3V3, OLED1.VDD, PIR1.VDD
  GND: U1.GND, OLED1.GND, PIR1.GND, A1.pin2
  N4: U1.D5, PIR1.SIG
  N5: U1.Vin, A1.pin1

custom parts:
  NodeMCU V1.0: ESP8266 based NodeMCU
  OLED 128x64 I2C Monochrome Display VDD-GND: OLED 128x64 I2C Monochrome Display. Note: there are two variants of this part, this one is the VDD GND SCK SDA variant. The other is GND VDD SCK SDA. Make sure you select the part that matches your module as using the incorrect part will probably destroy your module! In addition the mounting holes are marked on silkscreen but not by default drilled. If you want drilled mounting holes, copy a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
  yf-s401 flow sensor: Flow sensors sit in line with your water line, and uses a pinwheel sensor to measure how much liquid has moved through it.
